# Fritzing sketch Alarma Bluetooth JoseAngelPalomares (saved by Fritzing 0.8.7b)
breadboards: 1

parts:
  BT1 = Bluetooth HC-06u [package=THT]
  J1 = Piezo Speaker
  Parte1 = Arduino Uno (Rev3)
  IC1 = L293D [package=THT]
  R1 = Resistor [tolerance=±5% resistance=1M package=THT]
  R2 = Resistor [tolerance=±5% resistance=100k package=THT]
  M1 = DC Motor
  M2 = DC Motor
  LED1 = LED - 5mm [color="Red (633nm)" package="5 mm [THT]"]
  LED2 = LED - 5mm [color="Red (633nm)" package="5 mm [THT]"]  # not connected
  LED3 = LED - 5mm [color="White (8000K)" package="5 mm [THT]"]  # not connected
  LED4 = LED - 5mm [color="White (6500K)" package="5 mm [THT]"]  # not connected
  BAT1 = BC9VPC [package=bc9vpc]

nets:
  VCC: BT1.VCC, Parte1.5V, IC1.Enable_1, IC1.Enable_2, IC1.+V
  GND: BT1.GND, Parte1.GND, IC1.Out_1_(_Controlled_by_Enable_1_), M2.pin_2, BAT1.V+
  N1: BT1.TXD, Parte1.D0/RX
  N2: BT1.RXD, Parte1.D1/TX
  N3: J1.pin1, Parte1.D13/SCK
  N4: J1.pin2, Parte1.D3_PWM
  N5: Parte1.A0, R1.Pin_1, R2.Pin_0
  N6: Parte1.D9_PWM, IC1.In_1
  N7: Parte1.D10_PWM/SS, IC1.In_2
  N8: Parte1.D12/MISO, LED1.anode
  N9: Parte1.D5_PWM, IC1.In_4
  N10: Parte1.D6_PWM, IC1.In_3
  N11: Parte1.VIN, BAT1.V-
  N12: IC1.Out_2_(_Controlled_by_Enable_1_), M2.pin_1
  N13: IC1.+Vmotor, R1.Pin_0
  N14: IC1.Out_3_(_Controlled_by_Enable_2_), M1.pin_2
  N15: IC1.Out_4_(_Controlled_by_Enable_2_), M1.pin_1

custom parts:
  Bluetooth HC-06u: Bluetooth HC-06 - face up, pins down 16.5mm x 37.5mm PCB
