# Fritzing sketch DIAL_SECURITY (saved by Fritzing 0.9.3b)

parts:
  RE1 = KY-040 Rotary encoder [package=THT]
  Part1 = TM1637
  Part2 = Arduino Uno (Rev3) - ICSP
  J1 = Piezo Speaker
  LED1 = LEDs [package=led10mm]

nets:
  GND: RE1.GND, Part1.GND, Part2.GND, J1.pin1, LED1.C
  N1: RE1.SW, Part2.D6_PWM
  N2: RE1.DT, Part2.D5_PWM
  N3: RE1.CLK, Part2.D4
  VCC: Part1.VCC, Part2.5V
  N4: Part1.DIO, Part2.D9_PWM
  N5: Part1.CLK, Part2.D8
  N6: Part2.D2, J1.pin2
  N7: Part2.D3_PWM, LED1.A

custom parts:
  KY-040 Rotary encoder: KY-040 Rotary Encoder with switch on breakout borad from AZ Delivery
  TM1637: A 4 7-seg display
