# Fritzing sketch Hand Sanitizer (saved by Fritzing 0.9.3b)
breadboards: 1

parts:
  Part1 = Arduino Uno (Rev3)
  J1 = Basic Servo
  J2 = Infrared Proximity Sensor
  LED1 = smd LED [color="Blue (470nm)" package="0805 [SMD]"]
  LED2 = smd LED [color="Blue (470nm)" package="0805 [SMD]"]
  LED3 = smd LED [color="Blue (470nm)" package="0805 [SMD]"]
  LED4 = smd LED [color="Blue (470nm)" package="0805 [SMD]"]
  R1 = Resistor [tolerance=±5% resistance=100 package="0402 [SMD]"]
  J3 = Piezo Speaker
  R2 = Resistor [tolerance=±5% resistance=220 package="0402 [SMD]"]
  LCM1602_IIC1 = LCM1602 IIC [part_number="LCM1602 IIC" chip_label="LCM1602 IIC" package="DIP (Dual Inline) [THT]"]
  LCD1 = LCD screen

nets:
  N1: Part1.A4/SDA, LCM1602_IIC1.SDA
  N2: Part1.A5/SCL, LCM1602_IIC1.SCL
  N3: Part1.D8, J2.Vout
  N4: Part1.D9_PWM, J1.pulse
  N5: Part1.D10_PWM/SS, R1.Pin_0
  N6: Part1.D11_PWM/MOSI, R2.Pin_0
  VCC: Part1.5V, J1.vcc, LCM1602_IIC1.VCC
  GND: Part1.GND, J1.gnd, LED1.cathode, LED2.cathode, LED3.cathode, LED4.cathode, J3.pin1, LCM1602_IIC1.GND
  N7: LED1.anode, LED2.anode, LED3.anode, LED4.anode, R1.Pin_1
  N8: J3.pin2, R2.Pin_1
  VSS: LCM1602_IIC1.VSS, LCD1.VSS
  VDD: LCM1602_IIC1.VDD, LCD1.VDD
  N9: LCM1602_IIC1.V0, LCD1.V0
  N10: LCM1602_IIC1.RS, LCD1.RS
  N11: LCM1602_IIC1.RW, LCD1.R/W
  N12: LCM1602_IIC1.E, LCD1.E
  N13: LCM1602_IIC1.D0, LCD1.DB0
  N14: LCM1602_IIC1.D1, LCD1.DB1
  N15: LCM1602_IIC1.D2, LCD1.DB2
  N16: LCM1602_IIC1.D3, LCD1.DB3
  N17: LCM1602_IIC1.D4, LCD1.DB4
  N18: LCM1602_IIC1.D5, LCD1.DB5
  N19: LCM1602_IIC1.D6, LCD1.DB6
  N20: LCM1602_IIC1.D7, LCD1.DB7
  N21: LCM1602_IIC1.A, LCD1.LED+
  N22: LCM1602_IIC1.K, LCD1.LED-
  N23: LCM1602_IIC1.LED_A, LCM1602_IIC1.LED_B

custom parts:
  LCM1602 IIC: I2C-Module to use a 1602 or 2004 LCD on with the wire.h libory Serial LCD Modul
