# Fritzing sketch Pet Feeder (saved by Fritzing 0.9.3b)

parts:
  LCM1602_IIC1 = LCM1602 IIC [part_number="LCM1602 IIC" chip_label="LCM1602 IIC" package="DIP (Dual Inline) [THT]"]
  U1 = NodeMCU V1.0
  U2 = LCD-16X2 [package=lcd-16x2_noholes]
  J1 = Basic Servo

nets:
  VSS: LCM1602_IIC1.VSS, U2.VSS
  VDD: LCM1602_IIC1.VDD, U2.VDD
  N1: LCM1602_IIC1.V0, U2.VO
  N2: LCM1602_IIC1.RS, U2.RS
  N3: LCM1602_IIC1.RW, U2.R_W
  N4: LCM1602_IIC1.E, U2.E
  N5: LCM1602_IIC1.D0, U2.DB0
  N6: LCM1602_IIC1.D1, U2.DB1
  N7: LCM1602_IIC1.D2, U2.DB2
  N8: LCM1602_IIC1.D3, U2.DB3
  N9: LCM1602_IIC1.D4, U2.DB4
  N10: LCM1602_IIC1.D5, U2.DB5
  N11: LCM1602_IIC1.D6, U2.DB6
  N12: LCM1602_IIC1.D7, U2.DB7
  N13: LCM1602_IIC1.A, U2.A
  N14: LCM1602_IIC1.K, U2.K
  GND: LCM1602_IIC1.GND, U1.GND
  VCC: LCM1602_IIC1.VCC, U1.Vin, J1.vcc
  N15: LCM1602_IIC1.SDA, U1.D2
  N16: LCM1602_IIC1.SCL, U1.D1

custom parts:
  LCM1602 IIC: I2C-Module to use a 1602 or 2004 LCD on with the wire.h libory Serial LCD Modul
  NodeMCU V1.0: ESP8266 based NodeMCU
