# Fritzing sketch ROCHIK-IT (saved by Fritzing 0.9.3b)
breadboards: 3

parts:
  Part1 = RFID-RC522 [part_number=101218]
  LCD1 = LCD screen
  Raspberry_Pi1 = Raspberry Pi 2
  LCM1602_IIC1 = LCM1602 IIC [part_number="LCM1602 IIC" chip_label="LCM1602 IIC" package="DIP (Dual Inline) [THT]"]
  M1 = fc-51 [package=THT]
  J1 = Piezo Speaker

nets:
  N1: Part1.SDA, Raspberry_Pi1.GPIO8
  N2: Part1.SCK, Raspberry_Pi1.GPIO11
  N3: Part1.MOSI, Raspberry_Pi1.GPIO10
  N4: Part1.MISO, Raspberry_Pi1.GPIO9
  GND: Part1.GND, Raspberry_Pi1.GND, LCM1602_IIC1.GND, M1.pin1, M1.pin2, J1.pin1
  N5: Part1.RST, Raspberry_Pi1.GPIO25
  3.3V: Part1.3.3V, Raspberry_Pi1.3v3
  VSS: LCD1.VSS, LCM1602_IIC1.VSS
  VDD: LCD1.VDD, LCM1602_IIC1.VDD
  N6: LCD1.V0, LCM1602_IIC1.V0
  N7: LCD1.RS, LCM1602_IIC1.RS
  N8: LCD1.R/W, LCM1602_IIC1.RW
  N9: LCD1.E, LCM1602_IIC1.E
  N10: LCD1.DB0, LCM1602_IIC1.D0
  N11: LCD1.DB1, LCM1602_IIC1.D1
  N12: LCD1.DB2, LCM1602_IIC1.D2
  N13: LCD1.DB3, LCM1602_IIC1.D3
  N14: LCD1.DB4, LCM1602_IIC1.D4
  N15: LCD1.DB5, LCM1602_IIC1.D5
  N16: LCD1.DB6, LCM1602_IIC1.D6
  N17: LCD1.DB7, LCM1602_IIC1.D7
  N18: LCD1.LED+, LCM1602_IIC1.A
  N19: LCD1.LED-, LCM1602_IIC1.K
  N20: Raspberry_Pi1.GPIO2, LCM1602_IIC1.SDA
  N21: Raspberry_Pi1.GPIO3, LCM1602_IIC1.SCL
  N22: Raspberry_Pi1.GPIO19, J1.pin2
  5V: Raspberry_Pi1.5V, LCM1602_IIC1.VCC, M1.pin3

custom parts:
  LCM1602 IIC: I2C-Module to use a 1602 or 2004 LCD on with the wire.h libory Serial LCD Modul
