# Fritzing sketch RaspberryPI-RFID-RC522 (saved by Fritzing 0.9.3b)
circuit board: 8.46667cm x 5.64444cm

parts:
  Raspberry_Pi_1 = Raspberry Pi 3 [part_number=RPI-3-V1.2]
  MFRC523 = RFID-RC522 Reader

nets:
  3V3: Raspberry_Pi_1.3v3, Raspberry_Pi_1.3V3, MFRC523.3.3V
  N1: Raspberry_Pi_1.GIPO10, MFRC523.MOSI
  N2: Raspberry_Pi_1.GIPO9, MFRC523.MISO
  N3: Raspberry_Pi_1.GIPO11, MFRC523.SCK
  N4: Raspberry_Pi_1.GIPO8, MFRC523.SDA
  N5: Raspberry_Pi_1.GIPO25, MFRC523.RST
  GND: Raspberry_Pi_1.GND, MFRC523.GND
  N6: Raspberry_Pi_1.GIPO24, MFRC523.IRQ
