# Fritzing sketch Solar-panel-power-output (saved by Fritzing 0.8.7b)

parts:
  Part1 = Solar Cell
  Part2 = Current Sensor 5A
  Part3 = Arduino Uno (Rev3)
  LCM1602_IIC1 = LCM1602 IIC [part_number="LCM1602 IIC" chip_label="LCM1602 IIC" package="DIP (Dual Inline) [THT]"]
  LCD1 = LCD screen

nets:
  N1: Part1.+, Part2.2, Part2.OUT, Part3.A0
  GND: Part1.-, Part2.GND, Part3.GND, LCM1602_IIC1.GND
  N2: Part2.1, Part3.A1
  VCC: Part2.VCC, Part3.5V, LCM1602_IIC1.VCC
  N3: Part3.A4/SDA, LCM1602_IIC1.SDA
  N4: Part3.A5/SCL, LCM1602_IIC1.SCL
  VSS: LCM1602_IIC1.VSS, LCD1.VSS
  VDD: LCM1602_IIC1.VDD, LCD1.VDD
  N5: LCM1602_IIC1.V0, LCD1.V0
  N6: LCM1602_IIC1.RS, LCD1.RS
  N7: LCM1602_IIC1.RW, LCD1.R/W
  N8: LCM1602_IIC1.E, LCD1.E
  N9: LCM1602_IIC1.D0, LCD1.DB0
  N10: LCM1602_IIC1.D1, LCD1.DB1
  N11: LCM1602_IIC1.D2, LCD1.DB2
  N12: LCM1602_IIC1.D3, LCD1.DB3
  N13: LCM1602_IIC1.D4, LCD1.DB4
  N14: LCM1602_IIC1.D5, LCD1.DB5
  N15: LCM1602_IIC1.D6, LCD1.DB6
  N16: LCM1602_IIC1.D7, LCD1.DB7
  N17: LCM1602_IIC1.A, LCD1.LED+
  N18: LCM1602_IIC1.K, LCD1.LED-
  N19: LCM1602_IIC1.LED_A, LCM1602_IIC1.LED_B

custom parts:
  LCM1602 IIC: I2C-Module to use a 1602 or 2004 LCD on with the wire.h libory Serial LCD Modul
