# Fritzing sketch arduino-sim800l-fritzing (saved by Fritzing 0.8.7b)

parts:
  SIM800L_BO1 = SIM800L BO
  Part1 = Arduino Uno (Rev3)

nets:
  N1: SIM800L_BO1.PIN3, Part1.D4
  N2: SIM800L_BO1.pin_4, Part1.D2
  N3: SIM800L_BO1.pin_5, Part1.D3_PWM
