# Fritzing sketch cw (saved by Fritzing 0.9.3b)
breadboards: 2

parts:
  DHT1 = Humidity and Temperature Sensor DHT11
  U1 = ESP32-38PinWide [part_number=ESP32-38PinWide]
  LCM1602_IIC1 = LCM1602 IIC [part_number="LCM1602 IIC" chip_label="LCM1602 IIC" package="DIP (Dual Inline) [THT]"]
  Part1 = FC-28 Soil Hygrometer Module
  Part2 = FC-28 Soil Hygrometer Module - Probe
  U2 = LCD-16X2 [package=lcd-16x2]
  HC-SR04_Sensor_1 = HC-SR04 Ultrasonic Distance Sensor
  J1 = Piezo Speaker

nets:
  N1: DHT1.Vcc, DHT1.Data-signal, U1.3.3, U1.GPIO4
  GND: DHT1.GND_2, U1.GND, LCM1602_IIC1.VSS, LCM1602_IIC1.GND, Part1.GND, U2.VSS, HC-SR04_Sensor_1.GND, J1.pin1
  N2: U1.GPIO14, J1.pin2
  N3: U1.GPIO9, Part1.AO
  VCC: U1.VIN, LCM1602_IIC1.VCC, Part1.VCC, HC-SR04_Sensor_1.VCC
  N4: U1.GPIO5, HC-SR04_Sensor_1.ECHO
  N5: U1.GPIO18, HC-SR04_Sensor_1.TRIG
  N6: U1.GPIO21, LCM1602_IIC1.SDA
  N7: U1.GPIO22, LCM1602_IIC1.SCL
  VDD: LCM1602_IIC1.VDD, U2.VDD
  N8: LCM1602_IIC1.V0, U2.VO
  N9: LCM1602_IIC1.RS, U2.RS
  N10: LCM1602_IIC1.RW, U2.R_W
  N11: LCM1602_IIC1.E, U2.E
  N12: LCM1602_IIC1.D0, U2.DB0
  N13: LCM1602_IIC1.D1, U2.DB1
  N14: LCM1602_IIC1.D2, U2.DB2
  N15: LCM1602_IIC1.D3, U2.DB3
  N16: LCM1602_IIC1.D4, U2.DB4
  N17: LCM1602_IIC1.D5, U2.DB5
  N18: LCM1602_IIC1.D6, U2.DB6
  N19: LCM1602_IIC1.D7, U2.DB7
  N20: LCM1602_IIC1.A, U2.A
  N21: LCM1602_IIC1.K, U2.K
  N22: Part1.POS, Part2.POS
  N23: Part1.NEG, Part2.NEG

custom parts:
  Humidity and Temperature Sensor DHT11: Digital relative humidity & temperature sensor DHT11
  ESP32-38PinWide: Generic 38-Pin ESP32 with wide format (only access to one side of pins on a breadboard) based on Stephen Lilley's HiLetgo ESP-WROOM-32 ESP32 ESP-32S Development Board.
  LCM1602 IIC: I2C-Module to use a 1602 or 2004 LCD on with the wire.h libory Serial LCD Modul
  FC-28 Soil Hygrometer Module: The FC-28 is a soil hygrometer module that uses the Texas Instruments LM393 comparator chip to provide an analog measurement of soil humidity. The digital output is high when soil moisture is over a certain threshold, as determined by adjusting the potentiometer.
  FC-28 Soil Hygrometer Module - Probe: The FC-28 is a soil hygrometer module that uses the Texas Instruments LM393 comparator chip to provide an analog measurement of soil humidity.
