# Fritzing sketch cylinder brahim (saved by Fritzing 0.9.3b)
breadboards: 1

parts:
  Part3 = Arduino Nano (Rev3.0)
  LCM1602_IIC1 = LCM1602 IIC [part_number="LCM1602 IIC" chip_label="LCM1602 IIC" package="DIP (Dual Inline) [THT]"]
  U1 = LCD-16X2 [package=lcd-16x2_noholes]
  KY-1 = Keyes Relay [package=THT]
  J1 = Power Jack [package=power_jack_pth_lock]
  M1 = DC Motor

nets:
  GND: Part3.GND, LCM1602_IIC1.GND, KY-1.ground
  N1: Part3.D4, KY-1.signal
  5V: Part3.5V, LCM1602_IIC1.VCC, KY-1.power
  N2: Part3.A5, LCM1602_IIC1.SCL
  N3: Part3.A4, LCM1602_IIC1.SDA
  VSS: LCM1602_IIC1.VSS, U1.VSS
  VDD: LCM1602_IIC1.VDD, U1.VDD
  N4: LCM1602_IIC1.V0, U1.VO
  N5: LCM1602_IIC1.RS, U1.RS
  N6: LCM1602_IIC1.RW, U1.R_W
  N7: LCM1602_IIC1.E, U1.E
  N8: LCM1602_IIC1.D0, U1.DB0
  N9: LCM1602_IIC1.D1, U1.DB1
  N10: LCM1602_IIC1.D2, U1.DB2
  N11: LCM1602_IIC1.D3, U1.DB3
  N12: LCM1602_IIC1.D4, U1.DB4
  N13: LCM1602_IIC1.D5, U1.DB5
  N14: LCM1602_IIC1.D6, U1.DB6
  N15: LCM1602_IIC1.D7, U1.DB7
  N16: LCM1602_IIC1.A, U1.A
  N17: LCM1602_IIC1.K, U1.K
  N18: J1.GND, M1.pin_2

custom parts:
  LCM1602 IIC: I2C-Module to use a 1602 or 2004 LCD on with the wire.h libory Serial LCD Modul
  Keyes Relay: The Keyes 5V relay module is suitable for SCM development, home appliance control. It uses a 5V~12V TIL control signal which can control DC / AC signal.
