# Fritzing sketch lock_YlE65x0V02 (saved by Fritzing 0.9.3b)

parts:
  Part1 = Arduino Uno (Rev3)
  J1 = Basic Servo
  Part2 = RFID-RC522 [part_number=101218]

nets:
  N1: Part1.D9_PWM, Part2.RST
  N2: Part1.D10_PWM/SS, Part2.SDA
  N3: Part1.D11_PWM/MOSI, Part2.MOSI
  N4: Part1.D12/MISO, Part2.MISO
  N5: Part1.D13/SCK, Part2.SCK
  N6: Part1.D3_PWM, J1.pulse
  3V3: Part1.3V3, Part2.3.3V
  5V: Part1.5V, J1.vcc
  GND: Part1.GND, J1.gnd, Part2.GND
