# Fritzing sketch relay1 (saved by Fritzing 0.9.3b)

parts:
  8_Channel_Relay1 = 8 Channel Power Relay
  Part1 = Arduino Uno (Rev3)
  LED1 = LEDs [package=led10mm]

nets:
  GND: 8_Channel_Relay1.GND, Part1.GND
  N1: 8_Channel_Relay1.IN8, Part1.D8
  N2: 8_Channel_Relay1.VCC#17, Part1.5V
  N3: 8_Channel_Relay1.VCC#19, 8_Channel_Relay1.JD-VCC
  N4: 8_Channel_Relay1.COM, LED1.A

notes:
  Neutral
  Live
  Relay 8 (in8)
  Digital (PWM~) Pin 8

custom parts:
  8 Channel Power Relay: An 8 channel power relay. The module operates at 5V.
  LEDs: LEDs Standard schematic elements and footprints for 5mm, 3mm, 1206, and 0603 sized LEDs. 5mm - Spark Fun Electronics SKU : COM-00529 (and others)
